# Fritzing sketch NodeMCU-LedStripController (saved by Fritzing 0.9.3b)
circuit board: 5.67243cm x 5.61214cm
breadboards: 1

parts:
  NodeMCU = NodeMCU V1.0
  Red = MOSFET-NCHANNEL [package=to220v]
  Green = MOSFET-NCHANNEL [package=to220v]
  Blue = MOSFET-NCHANNEL [package=to220v]
  R_G_B_+ = female pin header, 4 pins [form="♀ (female)"]
  +_1_2_3_4_- = female pin header, 6 pins [form="♀ (female)"]
  Power = Power Jack [package=power_jack_pth_lock]
  8_Channel_Relay1 = 8 Channel Power Relay

nets:
  N1: NodeMCU.D2, Blue.G
  N2: NodeMCU.D3, Green.G
  N3: NodeMCU.D4, Red.G
  GND: NodeMCU.GND, Red.S, Green.S, Blue.S, +_1_2_3_4_-.pin6, Power.GND, 8_Channel_Relay1.GND
  N4: NodeMCU.D5, +_1_2_3_4_-.pin5, 8_Channel_Relay1.IN1
  N5: NodeMCU.D6, +_1_2_3_4_-.pin4, 8_Channel_Relay1.IN2
  N6: NodeMCU.D7, +_1_2_3_4_-.pin3, 8_Channel_Relay1.IN3
  N7: NodeMCU.D8, +_1_2_3_4_-.pin2, 8_Channel_Relay1.IN4
  VIN: NodeMCU.Vin, +_1_2_3_4_-.pin1, 8_Channel_Relay1.VCC
  N8: Red.D, R_G_B_+.pin4
  N9: Green.D, R_G_B_+.pin3
  N10: Blue.D, R_G_B_+.pin2
  N11: R_G_B_+.pin1, Power.PWR

custom parts:
  NodeMCU V1.0: ESP8266 based NodeMCU
  8 Channel Power Relay: An 8 channel power relay. The module operates at 5V.
